# Fritzing sketch ControllerCircuitDiagram (saved by Fritzing 0.9.3b)
circuit board: 8.46667cm x 5.64444cm
perfboards: 1

parts:
  LED2 = LED - 5mm [color="Red (633nm)" package="5 mm [THT]"]  # not connected
  R1 = Resistor [tolerance=±5% resistance=220 package="0805 [SMD]"]
  S1 = Pushbutton [package="[SMD]"]
  S2 = Pushbutton [package="[SMD]"]
  R2 = Resistor [tolerance=±5% resistance=10k package="0805 [SMD]"]  # not connected
  R3 = Resistor [tolerance=±5% resistance=10k package="0805 [SMD]"]  # not connected
  U1 = POT [package=pot_mammoth]
  R4 = Resistor [tolerance=±5% resistance=10k package="0805 [SMD]"]  # not connected
  LED3 = LED - 5mm [color="Red (633nm)" package="5 mm [THT]"]  # not connected
  R5 = Resistor [tolerance=±5% resistance=220 package="0805 [SMD]"]
  LED4 = LED - 5mm [color="Red (633nm)" package="5 mm [THT]"]  # not connected
  R6 = Resistor [tolerance=±5% resistance=220 package="0805 [SMD]"]
  S3 = Pushbutton [package="[SMD]"]
  S4 = Pushbutton [package="[SMD]"]
  R7 = Resistor [tolerance=±5% resistance=220 package="2010 [SMD]"]
  R7_2 = Resistor [tolerance=±5% resistance=10k package="2512 [SMD]"]

nets:
  N1: R1.Pin_0, U1.E, R5.Pin_0, R6.Pin_0
  N2: S1.Pin_1, S1.Pin_2
  N3: S1.Pin_3, S1.Pin_4
  N4: S2.Pin_1, S2.Pin_2
  N5: S2.Pin_3, S2.Pin_4
  N6: S3.Pin_1, S3.Pin_2
  N7: S3.Pin_3, S3.Pin_4
  N8: S4.Pin_1, S4.Pin_2
  N9: S4.Pin_3, S4.Pin_4
  N10: R7.Pin_0, R7_2.Pin_0
  N11: R7.Pin_1, R7_2.Pin_1

notes:
  servo indicator
  save, load
  switch
  rotate
  10
  light mode
